# Fritzing sketch RS (saved by Fritzing 0.9.2b)
circuit board: 15.0359cm x 10.1914cm
breadboards: 1

parts:
  S1 = Toggle Switch [package=THT]
  S2 = Toggle Switch [package=THT]
  R1 = Resistor [tolerance=±5% resistance=220 package=THT]
  LED1 = LED - 5mm [color="Red (633nm)" package="5 mm [THT]"]
  VCC1 = Battery
  M1 = DC Motor
  MD1 = TA7291P [package=HSIP10-P-2.54(THT)]
  MD2 = TA7291P [package=HSIP10-P-2.54(THT)]
  MD3 = TA7291P [package=HSIP10-P-2.54(THT)]
  M2 = DC Motor
  M3 = DC Motor
  VCC2 = Battery
  LED2 = LED - 5mm [color="Red (633nm)" package="5 mm [THT]"]
  R2 = Resistor [tolerance=±5% resistance=220 package=THT]
  esp = mystery part, 18 pins [chip_label="esp-wroom-02(full ver)"]
  arduino = mystery part, 28 pins [chip_label=ＡＥ－ＡＴＭＥＧＡ３２８－ＭＩＮＩ]
  R3 = Resistor [tolerance=±5% resistance=220 package=THT]
  MM-TXS01 = mystery part, 20 pins [chip_label=MM-TXS01]
  R4 = Resistor [tolerance=±5% resistance=220 package=THT]
  R5 = Resistor [tolerance=±5% resistance=220 package=THT]
  R6 = Resistor [tolerance=±5% resistance=220 package=THT]
  R8 = Resistor [tolerance=±5% resistance=220 package=THT]

nets:
  N1: S1.L1, R1.Pin_1, arduino.pin13
  N2: S1.COM, VCC1.+, VCC2.-, LED2.anode, esp.pin18, arduino.pin11, MM-TXS01.pin20
  N3: S2.COM, VCC2.+
  N4: S2.L2, MD1.Vs, MD3.Vs, R2.Pin_0
  N5: R1.Pin_0, LED1.cathode
  N6: LED1.anode, VCC1.-
  N7: M1.pin_1, MD1.OUT1
  N8: M1.pin_2, MD1.OUT2
  GND: MD1.GND, MD3.GND, MM-TXS01.pin11
  N9: MD1.Vref, MD1.IN2, arduino.pin26
  N10: MD1.IN1, arduino.pin27
  VCC: MD1.Vcc, MD2.Vcc, MD3.Vcc
  N11: MD2.OUT1, M2.pin_1
  N12: MD2.Vref, arduino.pin24
  N13: MD2.IN1, arduino.pin23
  N14: MD2.IN2, arduino.pin22
  N15: MD2.OUT2, M2.pin_2
  N16: MD3.OUT1, M3.pin_1
  N17: MD3.Vref, arduino.pin21
  N18: MD3.IN1, arduino.pin18
  N19: MD3.IN2, arduino.pin17
  N20: MD3.OUT2, M3.pin_2
  N21: LED2.cathode, R2.Pin_1
  N22: esp.pin1, R3.Pin_1, R4.Pin_1, R6.Pin_1, R8.Pin_1
  N23: esp.pin2, R6.Pin_0
  N24: esp.pin6, R5.Pin_0
  N25: esp.pin7, R4.Pin_0
  N26: esp.pin8, R3.Pin_0
  N27: esp.pin9, esp.pin13, MM-TXS01.pin10, R5.Pin_1
  N28: esp.pin10, MM-TXS01.pin2
  N29: esp.pin11, MM-TXS01.pin3
  N30: esp.pin15, R8.Pin_0
  N31: arduino.pin15, MM-TXS01.pin18
  N32: arduino.pin16, MM-TXS01.pin19

custom parts:
  TA7291P: The IC are Full-Bridge Driver. 4 modes available (CW / CCW / STOP / BRAKE) and PWM control. Output current:1.0 A (AVE.) 2.0 A (PEAK)
