# Fritzing sketch Untitled Sketch (saved by Fritzing 0.9.2b)
circuit board: 10.1482cm x 6.67421cm
breadboards: 1

parts:
  S1 = Toggle Switch [package=THT]
  S2 = Toggle Switch [package=THT]  # not connected
  R1 = Resistor [tolerance=±5% resistance=220 package=THT]
  LED1 = LED - 5mm [color="Red (633nm)" package="5 mm [THT]"]
  VCC1 = Battery
  M1 = DC Motor  # not connected
  S3 = Toggle Switch [package=THT]  # not connected
  S4 = Toggle Switch [package=THT]  # not connected
  U1 = mystery part, 28 pins [chip_label=ＡＥ－ＡＴＭＥＧＡ３２８－ＭＩＮＩ]  # not connected

nets:
  N1: S1.L1, R1.Pin_1
  N2: S1.L2, VCC1.+
  N3: R1.Pin_0, LED1.cathode
  N4: LED1.anode, VCC1.-
